// Digital circuit LOAD.dig as structural Verilog
module LOAD (
  input  [63:0] Dout,
  input  [63:0] TA,
  input  [1:0] MSZ
);

  wire [31:0] multiplexer_1_out;
  wire [63:0] bitextender_1_out;

  Multiplexer #(.Bits(32)) multiplexer_1 (.sel(TA[2]), .in_0(Dout[31:0]), .in_1(Dout[63:32]), .out(multiplexer_1_out));
  BitExtender #(.inputBits(32), .outputBits(64)) bitextender_1 (.in(multiplexer_1_out), .out(bitextender_1_out));
  Multiplexer #(.Selector_Bits(2), .Bits(64)) multiplexer_2 (
    .sel(MSZ), .in_0(Dout), .in_1(bitextender_1_out), .in_2({64{1'b0}}), .in_3({64{1'b0}}));  // open: out
endmodule
