// Digital circuit Store.dig as structural Verilog
module Store (
  input  [63:0] Dout,
  input  [63:0] RD1,
  input  [63:0] TA,
  input  [1:0] MSZ,
  output [63:0] Din,
  output [4:0] A
);

  wire [63:0] multiplexer_1_out;

  Multiplexer #(.Bits(64)) multiplexer_1 (
    .sel(TA[2]), .in_0({Dout[63:32], RD1[31:0]}), .in_1({RD1[31:0], Dout[31:0]}), .out(multiplexer_1_out));
  Multiplexer #(.Selector_Bits(2), .Bits(64)) multiplexer_2 (
    .sel(MSZ), .in_0(RD1), .in_1(multiplexer_1_out), .in_2({64{1'b0}}), .in_3({64{1'b0}}), .out(Din));

  assign A = TA[7:3];

  // Other names for the same wires on the sheet: w0[31:0] = Dout[31:0]; w1[31:0] = Dout[63:32]; wn[31:0] = RD1[31:0]
endmodule
